// Logisim project Ctl_Conditional.circ as structural Verilog: 1 circuit, main circuit Conditional
module Conditional (
  input  Enable,
  input  [15:0] Instruction,
  input  Z,
  input  C,
  input  N,
  input  V,
  output [10:0] Offset,
  output Verified
);

  wire and_1_out, and_2_out, comparator_1_eq, comparator_1_gt, comparator_1_lt, multiplexer_1_out, not_1_out,
       not_2_out, not_3_out, not_4_out, not_5_out, not_6_out, or_1_out, or_2_out, or_3_out, or_4_out;
  wire [10:0] bit_extender_1_out, bit_extender_2_out, multiplexer_2_out;

  not not_1 (not_1_out, Z);
  not not_2 (not_2_out, C);
  not not_3 (not_3_out, N);
  not not_4 (not_4_out, V);
  and and_1 (and_1_out, not_1_out, C);
  or or_1 (or_1_out, Z, not_5_out);
  not not_5 (not_5_out, C);
  Comparator #(.width(1)) comparator_1 (.a(N), .b(V), .gt(comparator_1_gt), .eq(comparator_1_eq), .lt(comparator_1_lt));
  not not_6 (not_6_out, Z);
  or or_2 (or_2_out, comparator_1_gt, comparator_1_lt);
  and and_2 (and_2_out, comparator_1_eq, not_6_out);
  or or_3 (or_3_out, or_2_out, Z);
  Multiplexer #(.select(4)) multiplexer_1 (
    .in0(Z), .in1(not_1_out), .in2(C), .in3(not_2_out), .in4(N), .in5(not_3_out), .in6(V), .in7(not_4_out),
    .in8(and_1_out), .in9(or_1_out), .in10(comparator_1_eq), .in11(or_2_out), .in12(and_2_out),
    .in13(or_3_out), .in14(1'b1), .in15(1'b0), .out(multiplexer_1_out), .sel(Instruction[11:8]));
  or or_4 (or_4_out, Instruction[13], multiplexer_1_out);
  and and_3 (Verified, Enable, or_4_out);
  assign bit_extender_1_out = {{3{Instruction[7]}}, Instruction[7:0]};  // Bit_Extender bit_extender_1
  Multiplexer #(.width(11)) multiplexer_2 (
    .in0(bit_extender_1_out), .in1(Instruction[10:0]), .out(multiplexer_2_out), .sel(Instruction[13]));
  assign bit_extender_2_out = {{10{Verified}}, Verified};  // Bit_Extender bit_extender_2
  assign Offset = multiplexer_2_out & bit_extender_2_out;  // AND_Gate and_4, 11 bits wide

  // Other names for the same wires on the sheet: imm8[7:0] = Instruction[7:0]; imm11[10:0] = Instruction[10:0]
endmodule
