// Logisim project Ctl_Data_Processing.circ as structural Verilog: 3 circuits, main circuit Data_Processing
module Data_Processing (
  input  [15:0] Instruction,
  input  Enable,
  output [2:0] Rd,
  output [2:0] Rm,
  output [2:0] Rn,
  output [3:0] ALU_Opcode,
  output [3:0] Flags_Update_Mask
);

  wire or_1_out, selecteur_op_exceptions_1_mul, selecteur_op_exceptions_1_rsb;
  wire [2:0] multiplexer_1_out, multiplexer_2_out;
  wire [3:0] flags_up_1_nzcv;

  selecteur_op_exceptions selecteur_op_exceptions_1 (
    .op(Instruction[9:6]), .MUL(selecteur_op_exceptions_1_mul), .RSB(selecteur_op_exceptions_1_rsb));
  or or_1 (or_1_out, selecteur_op_exceptions_1_mul, selecteur_op_exceptions_1_rsb);
  Multiplexer #(.width(3)) multiplexer_1 (
    .in0(Instruction[5:3]), .in1(Instruction[2:0]), .out(multiplexer_1_out),
    .sel(selecteur_op_exceptions_1_mul));
  Multiplexer #(.width(3)) multiplexer_2 (
    .in0(Instruction[2:0]), .in1(Instruction[5:3]), .out(multiplexer_2_out), .sel(or_1_out));
  Multiplexer #(.width(3)) multiplexer_3 (.in0(3'b000), .in1(Instruction[2:0]), .out(Rd), .sel(Enable));
  flags_up flags_up_1 (.Code_op(Instruction[9:6]), .NZCV(flags_up_1_nzcv));
  Multiplexer #(.width(4)) multiplexer_4 (.in0(4'b0000), .in1(Instruction[9:6]), .out(ALU_Opcode), .sel(Enable));
  Multiplexer #(.width(3)) multiplexer_5 (.in0(3'b000), .in1(multiplexer_1_out), .out(Rm), .sel(Enable));
  Multiplexer #(.width(3)) multiplexer_6 (.in0(3'b000), .in1(multiplexer_2_out), .out(Rn), .sel(Enable));
  Multiplexer #(.width(4)) multiplexer_7 (.in0(4'b0000), .in1(flags_up_1_nzcv), .out(Flags_Update_Mask), .sel(Enable));

  // Other names for the same wires on the sheet: Code_OP[3:0] = Instruction[9:6]

  // Notes on the sheet:
  //   Pull output low on Enable = 0
endmodule

module selecteur_op_exceptions (
  input  [3:0] op,
  output MUL,
  output RSB
);

  wire not_1_out, not_2_out;

  not not_1 (not_1_out, op[2]);
  not not_2 (not_2_out, op[1]);
  and and_1 (MUL, op[3], op[2], not_2_out, op[0]);
  and and_2 (RSB, op[3], not_1_out, not_2_out, op[0]);
endmodule

module flags_up (
  input  [3:0] Code_op,
  output [3:0] NZCV
);

  wire and_1_out, and_2_out, and_3_out, and_4_out, not_1_out, not_2_out, not_3_out, not_4_out;

  not not_1 (not_1_out, Code_op[3]);
  not not_2 (not_2_out, Code_op[2]);
  not not_3 (not_3_out, Code_op[1]);
  not not_4 (not_4_out, Code_op[0]);
  or or_1 (NZCV[1], not_1_out, not_2_out, not_4_out, Code_op[1]);
  and and_1 (and_1_out, not_1_out, Code_op[2], not_3_out, Code_op[0]);
  and and_2 (and_2_out, not_1_out, Code_op[2], Code_op[1], not_4_out);
  and and_3 (and_3_out, Code_op[3], not_2_out, Code_op[0]);
  and and_4 (and_4_out, Code_op[3], not_2_out, Code_op[1]);
  or or_2 (NZCV[0], and_1_out, and_2_out, and_3_out, and_4_out);

  assign NZCV[3:2] = 2'b11;
endmodule
