// Logisim project Ctl_Load_Store.circ as structural Verilog: 1 circuit, main circuit Load_Store
module Load_Store (
  input  Enable,
  input  [15:0] Instruction,
  input  Clk,
  input  Reset,
  input  [31:0] Stack_Pointer,
  input  [31:0] B_Bus,
  input  [31:0] A_Bus,
  output Store,
  output Load,
  output PC_Hold,
  output [2:0] Rd,
  output [2:0] Rn,
  output [2:0] Rm,
  output [31:0] RAM_Addr,
  output [3:0] Alu_Opcode
);

  wire and_2_out, and_3_out, and_4_out, and_5_out, and_6_out, d_ff_1_q, or_1_out, or_2_out, or_3_out,
       or_4_out, or_5_out, PC_H, R_Offset_E;
  wire [2:0] multiplexer_7_out, multiplexer_8_out, multiplexer_9_out, multiplexer_10_out, multiplexer_12_out,
       Rm_t, Rt;
  wire [31:0] adder_1_out, Base, bit_extender_1_out, bit_extender_2_out, multiplexer_1_out,
       multiplexer_5_out, multiplexer_11_out, Offset, register_1_q, shifter_1_out, shifter_2_out;

  and and_1 (R_Offset_E, ~Instruction[15], Instruction[14], ~Instruction[13], Instruction[12]);  // AND_Gate
  Multiplexer #(.width(32)) multiplexer_1 (.in0(B_Bus), .in1(A_Bus), .out(multiplexer_1_out), .sel(R_Offset_E));
  Multiplexer #(.width(3)) multiplexer_2 (
    .in0(Instruction[10:8]), .in1(Instruction[2:0]), .out(Rt), .sel(Instruction[14]));
  Shifter #(.shift("ar"), .width(32)) shifter_1 (.in(multiplexer_1_out), .\dist (5'b00010), .out(shifter_1_out));
  Multiplexer #(.width(3)) multiplexer_3 (.in0(Instruction[5:3]), .in1(Instruction[8:6]), .out(Rm_t), .sel(R_Offset_E));
  assign bit_extender_1_out = {{24{Instruction[7]}}, Instruction[7:0]};  // Bit_Extender bit_extender_1
  assign bit_extender_2_out = {{27{Instruction[10]}}, Instruction[10:6]};  // Bit_Extender bit_extender_2
  Shifter #(.shift("ar"), .width(32)) shifter_2 (.in(B_Bus), .\dist (5'b00010), .out(shifter_2_out));
  Multiplexer #(.width(32)) multiplexer_4 (.in0(Stack_Pointer), .in1(shifter_1_out), .out(Base), .sel(Instruction[14]));
  Multiplexer #(.width(32)) multiplexer_5 (
    .in0(bit_extender_2_out), .in1(shifter_2_out), .out(multiplexer_5_out), .sel(R_Offset_E));
  Multiplexer #(.width(32)) multiplexer_6 (
    .in0(bit_extender_1_out), .in1(multiplexer_5_out), .out(Offset), .sel(Instruction[14]));
  Adder #(.width(32)) adder_1 (.a(Base), .b(Offset), .out(adder_1_out));  // open: cin, cout
  Multiplexer #(.width(3)) multiplexer_7 (
    .in0(Instruction[5:3]), .in1(Rm_t), .out(multiplexer_7_out), .sel(R_Offset_E));
  and and_2 (and_2_out, Instruction[14], PC_H);
  Multiplexer #(.width(3)) multiplexer_8 (
    .in0(Instruction[5:3]), .in1(Rm_t), .out(multiplexer_8_out), .sel(R_Offset_E));
  Register #(.width(32)) register_1 (.D(adder_1_out), .en(and_5_out), .clk(Clk), .Q(register_1_q), .clr(or_1_out));
  or or_1 (or_1_out, Reset, ~Enable);  // OR_Gate
  and and_3 (and_3_out, or_3_out, ~d_ff_1_q);  // AND_Gate
  D_Flip_Flop #(.trigger("falling")) d_ff_1 (
    .D(and_3_out), .clk(Clk), .Q(d_ff_1_q), .Qn(PC_H), .reset(or_2_out));  // open: preset
  or or_2 (or_2_out, Reset, ~Enable, ~or_3_out);  // OR_Gate
  Multiplexer #(.width(3)) multiplexer_9 (.in0(Rt), .in1(multiplexer_7_out), .out(multiplexer_9_out), .sel(and_2_out));
  Multiplexer #(.width(3)) multiplexer_10 (
    .in0(multiplexer_9_out), .in1(multiplexer_8_out), .out(multiplexer_10_out), .sel(and_4_out));
  and and_4 (and_4_out, Instruction[14], Instruction[11]);
  and and_5 (and_5_out, R_Offset_E, ~Instruction[11]);  // AND_Gate
  or or_3 (or_3_out, R_Offset_E, Instruction[11]);
  or or_4 (or_4_out, d_ff_1_q, ~R_Offset_E);  // OR_Gate
  and and_6 (and_6_out, or_5_out, R_Offset_E);
  or or_5 (or_5_out, PC_H, Instruction[11]);
  Multiplexer #(.width(32)) multiplexer_11 (
    .in0(adder_1_out), .in1(register_1_q), .out(multiplexer_11_out), .sel(and_5_out));
  Multiplexer #(.width(3)) multiplexer_12 (.in0(Rt), .in1(Instruction[5:3]), .out(multiplexer_12_out), .sel(and_6_out));
  and and_7 (Store, Enable, or_4_out, ~Instruction[11]);  // AND_Gate
  and and_8 (Load, Enable, Instruction[11], d_ff_1_q);
  and and_9 (PC_Hold, Enable, or_3_out, PC_H);
  Multiplexer #(.width(3)) multiplexer_13 (.in0(3'b000), .in1(multiplexer_9_out), .out(Rd), .sel(Enable));
  Multiplexer #(.width(3)) multiplexer_14 (.in0(3'b000), .in1(multiplexer_10_out), .out(Rn), .sel(Enable));
  Multiplexer #(.width(3)) multiplexer_15 (.in0(3'b000), .in1(multiplexer_12_out), .out(Rm), .sel(Enable));
  Multiplexer #(.width(32)) multiplexer_16 (.in0({32{1'b0}}), .in1(multiplexer_11_out), .out(RAM_Addr), .sel(Enable));
  Multiplexer #(.width(4)) multiplexer_17 (.in0(4'b0000), .in1(4'b1000), .out(Alu_Opcode), .sel(Enable));

  // Other names for the same wires on the sheet: Clock = Clk; Imm8[7:0] = Instruction[7:0];
  //   Rn_t[2:0] = Instruction[5:3]; Imm5[4:0] = Instruction[10:6]; Load_t = Instruction[11];
  //   Is_Register = Instruction[14]; R_Offset[31:0] = B_Bus

  // Notes on the sheet:
  //   Instruction: pull=down
  //   Delay load and hold PC for 1 cycle for the RAM to send out requested data 
endmodule
