// Logisim project Ctl_Opcode_Decoder.circ as structural Verilog: 1 circuit, main circuit Opcode_Decoder
module Opcode_Decoder (
  input  [5:0] Opcode,
  output Shift,
  output Data_Processing,
  output Load_Store,
  output SP_Address,
  output Conditional,
  output SP_Relative_Address
);

  wire and_3_out, and_4_out, and_5_out, and_7_out, and_8_out, NB0, NB1, NB2, NB3, NB4, NB5;

  not not_1 (NB0, Opcode[0]);
  not not_2 (NB1, Opcode[1]);
  not not_3 (NB2, Opcode[2]);
  not not_4 (NB3, Opcode[3]);
  not not_5 (NB4, Opcode[4]);
  not not_6 (NB5, Opcode[5]);
  and and_1 (Shift, NB5, NB4);
  and and_2 (Data_Processing, NB5, Opcode[4], NB3, NB2, NB1, NB0);
  and and_3 (and_3_out, Opcode[5], NB4, NB3, Opcode[2]);
  and and_4 (and_4_out, NB5, Opcode[4], Opcode[3]);
  and and_5 (and_5_out, NB5, Opcode[4], NB3, Opcode[2]);
  and and_6 (SP_Address, Opcode[5], NB4, Opcode[3], Opcode[2]);
  and and_7 (and_7_out, Opcode[5], Opcode[4], NB3, Opcode[2]);
  and and_8 (and_8_out, Opcode[5], Opcode[4], Opcode[3], NB2, NB1);
  and and_9 (SP_Relative_Address, Opcode[5], NB4, Opcode[3], NB2, Opcode[1]);
  or or_1 (Load_Store, and_3_out, and_4_out, and_5_out);
  or or_2 (Conditional, and_7_out, and_8_out);

  // Other names for the same wires on the sheet: B0 = Opcode[0]; B1 = Opcode[1]; B2 = Opcode[2]; B3 = Opcode[3];
  //   B4 = Opcode[4]; B5 = Opcode[5]

  // Notes on the sheet:
  //   Shift, add, sub, mov
  //   Data Processing
  //   Load/Store
  //   SP Address
  //   Conditional branch
endmodule
