// Logisim project Ctl_SP_Relative_Address.circ as structural Verilog: 1 circuit, main circuit SP_Relative_Addr
module SP_Relative_Addr (
  input  Enable,
  input  [15:0] Instruction,
  input  [31:0] SP,
  output [2:0] Rd,
  output Imm32_Enable,
  output [31:0] Imm32,
  output [3:0] ALU_Opcode
);

  wire [31:0] adder_1_out, bit_extender_1_out, negator_1_out, shifter_1_out, shifter_2_out;

  assign bit_extender_1_out = {{24{1'b0}}, Instruction[7:0]};  // Bit_Extender bit_extender_1
  Shifter #(.width(32)) shifter_1 (.in(SP), .\dist (5'b00010), .out(shifter_1_out));
  Shifter #(.shift("lr"), .width(32)) shifter_2 (.in(bit_extender_1_out), .\dist (5'b00010), .out(shifter_2_out));
  Adder #(.width(32)) adder_1 (.a(shifter_2_out), .b(shifter_1_out), .out(adder_1_out), .cin(1'b0));  // open: cout
  Negator #(.width(32)) negator_1 (.in(adder_1_out), .out(negator_1_out));
  Multiplexer #(.width(3)) multiplexer_1 (.in0(3'b000), .in1(Instruction[10:8]), .out(Rd), .sel(Enable));
  Multiplexer #(.width(32)) multiplexer_2 (.in0({32{1'b0}}), .in1(negator_1_out), .out(Imm32), .sel(Enable));
  Multiplexer #(.width(4)) multiplexer_3 (.in0(4'b0000), .in1(4'b1001), .out(ALU_Opcode), .sel(Enable));

  assign Imm32_Enable = Enable;
endmodule
