// Logisim project Ctl_Shift_Add_Sub_Mov.circ as structural Verilog: 6 circuits, main circuit Flag_update
module Shift_Add_Sub_Mov (
  input  Enable,
  input  [15:0] Instruction,
  output [3:0] Flags_Update_Mask,
  output Carry,
  output Imm32_Enable,
  output [2:0] Rm,
  output [2:0] Rn,
  output [2:0] Rd,
  output [4:0] Imm5,
  output [31:0] Imm32,
  output [3:0] ALU_Opcode
);

  wire calccarry_1_c, imm_1_imm32_e;
  wire [2:0] rx_1_rd, rx_1_rm, rx_1_rn;
  wire [3:0] flag_update_1_flag, opcode_1_aluop;
  wire [4:0] imm_1_imm5_s;
  wire [31:0] imm_1_imm32;

  Flag_update flag_update_1 (.Op(Instruction[13:11]), .Flag(flag_update_1_flag));
  CalcCarry calccarry_1 (.Op(Instruction[13:11]), .IsSub(Instruction[9]), .C(calccarry_1_c));
  Rx rx_1 (.Op(Instruction[13:11]), .Data(Instruction[10:0]), .Rm(rx_1_rm), .Rd(rx_1_rd), .Rn(rx_1_rn));
  Imm imm_1 (
    .Op(Instruction[13:11]), .IsRegister(Instruction[10]), .Imm3(Instruction[8:6]), .Imm8(Instruction[7:0]),
    .Imm5_E(Instruction[10:6]), .Imm32_E(imm_1_imm32_e), .Imm32(imm_1_imm32), .Imm5_S(imm_1_imm5_s));
  OpCode opcode_1 (.Op(Instruction[13:11]), .Sub(Instruction[9]), .AluOp(opcode_1_aluop));
  Multiplexer #(.width(4)) multiplexer_1 (
    .in0(4'b0000), .in1(flag_update_1_flag), .out(Flags_Update_Mask), .sel(Enable));
  Multiplexer multiplexer_2 (.in0(1'b0), .in1(calccarry_1_c), .out(Carry), .sel(Enable));
  Multiplexer multiplexer_3 (.in0(1'b0), .in1(imm_1_imm32_e), .out(Imm32_Enable), .sel(Enable));
  Multiplexer #(.width(3)) multiplexer_4 (.in0(3'b000), .in1(rx_1_rm), .out(Rm), .sel(Enable));
  Multiplexer #(.width(3)) multiplexer_5 (.in0(3'b000), .in1(rx_1_rn), .out(Rn), .sel(Enable));
  Multiplexer #(.width(3)) multiplexer_6 (.in0(3'b000), .in1(rx_1_rd), .out(Rd), .sel(Enable));
  Multiplexer #(.width(5)) multiplexer_7 (.in0({5{1'b0}}), .in1(imm_1_imm5_s), .out(Imm5), .sel(Enable));
  Multiplexer #(.width(32)) multiplexer_8 (.in0({32{1'b0}}), .in1(imm_1_imm32), .out(Imm32), .sel(Enable));
  Multiplexer #(.width(4)) multiplexer_9 (.in0(4'b0000), .in1(opcode_1_aluop), .out(ALU_Opcode), .sel(Enable));

  // Other names for the same wires on the sheet: Op[2:0] = Instruction[13:11]

  // Notes on the sheet:
  //   Note: ALU uses Rn register for shifts. Use Rn instead of Rm for shifts (immediate) here too
  //   Note 3: Imm32_Enable forces the use of the immediate for Rm register
  //   Note 2: MOV uses RSB ALU opcode with Imm8 reversed so that it is copied to output register
  //   Pull output low on Enable = 0
  //   only ADD and SUB use Rm
  //   Enable carry for SUB since it is reversed in ALU
  //   ALU will use Imm32 instead of Rm
endmodule

module Flag_update (
  input  [2:0] Op,
  output [3:0] Flag
);

  wire and_1_out, and_2_out, and_3_out, not_1_out;

  not not_1 (not_1_out, Op[2]);
  or or_1 (Flag[1], not_1_out, Op[0], Op[1]);
  and and_1 (and_1_out, Op[1], Op[0]);
  and and_2 (and_2_out, Op[2], Op[0]);
  and and_3 (and_3_out, Op[2], Op[1]);
  or or_2 (Flag[0], and_1_out, and_2_out, and_3_out);

  assign Flag[3:2] = 2'b11;
endmodule

module Imm (
  input  [2:0] Op,
  input  IsRegister,
  input  [2:0] Imm3,
  input  [7:0] Imm8,
  input  [4:0] Imm5_E,
  output Imm32_E,
  output [31:0] Imm32,
  output [4:0] Imm5_S
);

  wire and_1_out, and_2_out, and_3_out, and_4_out, not_1_out, not_2_out, not_3_out, or_1_out;
  wire [31:0] bit_extender_1_out, bit_extender_2_out, multiplexer_1_out, multiplexer_2_out, negator_1_out;

  not not_1 (not_1_out, Op[1]);
  not not_2 (not_2_out, Op[0]);
  not not_3 (not_3_out, Op[2]);
  assign bit_extender_1_out = {{29{1'b0}}, Imm3};  // Bit_Extender bit_extender_1
  assign bit_extender_2_out = {{24{1'b0}}, Imm8};  // Bit_Extender bit_extender_2
  and and_1 (and_1_out, Op[0], Op[1], IsRegister);
  and and_2 (and_2_out, not_2_out, not_1_out);
  Multiplexer #(.width(32)) multiplexer_1 (
    .in0(bit_extender_2_out), .in1(negator_1_out), .out(multiplexer_1_out), .sel(and_2_out));
  Negator #(.width(32)) negator_1 (.in(bit_extender_2_out), .out(negator_1_out));
  and and_3 (and_3_out, not_3_out, not_1_out);
  or or_1 (or_1_out, and_3_out, and_4_out);
  Multiplexer #(.width(32)) multiplexer_2 (
    .in0(bit_extender_1_out), .in1(multiplexer_1_out), .out(multiplexer_2_out), .sel(Op[2]));
  and and_4 (and_4_out, not_2_out, not_3_out);
  Multiplexer #(.width(5)) multiplexer_3 (.in0({5{1'b0}}), .in1(Imm5_E), .out(Imm5_S), .sel(or_1_out));
  or or_2 (Imm32_E, Op[2], and_1_out);
  Multiplexer #(.width(32)) multiplexer_4 (.in0({32{1'b0}}), .in1(multiplexer_2_out), .out(Imm32), .sel(Imm32_E));
endmodule

module CalcCarry (
  input  [2:0] Op,
  input  IsSub,
  output C
);

  wire and_1_out, and_2_out;

  and and_1 (and_1_out, Op[1], Op[0], IsSub);
  and and_2 (and_2_out, Op[2], Op[1], Op[0]);
  or or_1 (C, and_1_out, and_2_out);
endmodule

module Rx (
  input  [2:0] Op,
  input  [10:0] Data,
  output [2:0] Rm,
  output [2:0] Rd,
  output [2:0] Rn
);

  wire and_1_out, and_2_out, and_3_out, and_4_out, or_1_out, or_2_out;
  wire [2:0] multiplexer_1_out, multiplexer_2_out;

  Multiplexer #(.width(3)) multiplexer_1 (.in0(Data[8:6]), .in1(3'b000), .out(multiplexer_1_out), .sel(Data[10]));
  Multiplexer #(.width(3)) multiplexer_2 (.in0(3'b000), .in1(Data[10:8]), .out(multiplexer_2_out), .sel(and_1_out));
  and and_1 (and_1_out, Op[1], Op[2]);
  and and_2 (and_2_out, Op[0], Op[1], ~Op[2]);  // AND_Gate
  and and_3 (and_3_out, ~Op[0], ~Op[2]);  // AND_Gate
  and and_4 (and_4_out, ~Op[2], ~Op[1]);  // AND_Gate
  Multiplexer #(.width(3)) multiplexer_3 (.in0(multiplexer_1_out), .in1(Data[5:3]), .out(Rm), .sel(or_2_out));
  Multiplexer #(.width(3)) multiplexer_4 (.in0(Data[2:0]), .in1(Data[10:8]), .out(Rd), .sel(Op[2]));
  Multiplexer #(.width(3)) multiplexer_5 (.in0(multiplexer_2_out), .in1(Data[5:3]), .out(Rn), .sel(or_1_out));
  or or_1 (or_1_out, and_2_out, or_2_out);
  or or_2 (or_2_out, and_3_out, and_4_out);
endmodule

module OpCode (
  input  [2:0] Op,
  input  Sub,
  output [3:0] AluOp
);

  wire and_2_out, and_3_out, and_4_out, and_5_out, and_6_out, and_7_out, not_1_out, not_2_out, not_3_out,
       not_4_out;

  not not_1 (not_1_out, Op[2]);
  not not_2 (not_2_out, Op[1]);
  not not_3 (not_3_out, Op[0]);
  not not_4 (not_4_out, Sub);
  and and_1 (AluOp[3], Op[2], not_2_out);
  and and_2 (and_2_out, not_1_out, not_2_out);
  and and_3 (and_3_out, Op[0], Sub);
  and and_4 (and_4_out, Op[2], Op[0]);
  and and_5 (and_5_out, not_1_out, not_2_out, Op[0]);
  and and_6 (and_6_out, not_1_out, Op[0], not_4_out);
  and and_7 (and_7_out, Op[2], not_3_out);
  or or_1 (AluOp[1], and_2_out, and_3_out, and_4_out);
  or or_2 (AluOp[0], and_5_out, and_6_out, and_7_out);

  assign AluOp[2] = Op[1];
endmodule
