// Logisim project parm.circ as structural Verilog
module sommateur_1_bit (
  input  A,
  input  B,
  input  R_E,
  output S,
  output R_S
);

  wire and_1_out, and_2_out, xor_1_out;

  and and_1 (and_1_out, B, A);
  xor xor_1 (xor_1_out, A, B);
  and and_2 (and_2_out, xor_1_out, R_E);
  xor xor_2 (S, xor_1_out, R_E);
  or or_1 (R_S, and_2_out, and_1_out);
endmodule

module sommateur_32_bits (
);

  wire sommateur_1_bit_1_r_s, sommateur_1_bit_1_s;

  sommateur_1_bit sommateur_1_bit_1 (.S(sommateur_1_bit_1_s), .R_S(sommateur_1_bit_1_r_s));  // open: A, B, R_E
  sommateur_1_bit sommateur_1_bit_2 (.R_E(sommateur_1_bit_1_r_s));  // open: A, B, S, R_S
endmodule
